# Fritzing sketch 13_LED_RGB (saved by Fritzing 0.9.3b)
breadboards: 1

parts:
  Mod1 = KY-016 RGB Full Color LED Module [package="Breakout board"]
  S1 = Pushbutton [package="[THT]"]
  S2 = Pushbutton [package="[THT]"]
  S3 = Pushbutton [package="[THT]"]
  R1 = Resistor [tolerance=±5% resistance=220 package=THT]
  R2 = Resistor [tolerance=±5% resistance=220 package=THT]
  R3 = Resistor [tolerance=±5% resistance=220 package=THT]
  Componente1 = Arduino Uno (Rev3)

nets:
  N1: Mod1.R, Componente1.D11_PWM/MOSI
  N2: Mod1.G, Componente1.D12/MISO
  N3: Mod1.B, Componente1.D13/SCK
  N4: Mod1.-, R1.Pin_1, R2.Pin_1, R3.Pin_1, Componente1.GND
  N5: S1.Pin_1, S1.Pin_2, S2.Pin_1, S2.Pin_2, S3.Pin_1, S3.Pin_2, Componente1.5V
  N6: S1.Pin_3, S1.Pin_4, R1.Pin_0, Componente1.D5_PWM
  N7: S2.Pin_3, S2.Pin_4, R3.Pin_0, Componente1.D6_PWM
  N8: S3.Pin_3, S3.Pin_4, R2.Pin_0, Componente1.D7

custom parts:
  KY-016 RGB Full Color LED Module: KY-016 Arduino full color 5mm RGB LED, different colors can be obtained by mixing the three primary colors.
