# Fritzing sketch 7_Fuego (saved by Fritzing 0.9.3b)
breadboards: 1

parts:
  Mod1 = KY-026 Flame Sensor Module [package="Breakout board"]
  LED1 = LED - 5mm [color="Red (633nm)" package="5 mm [THT]"]
  Componente1 = Arduino Uno (Rev3)
  R1 = Resistor [tolerance=±5% resistance=220 package=THT]

nets:
  N1: Mod1.G, Componente1.GND, R1.Pin_1
  N2: Mod1.+, Componente1.5V
  N3: LED1.cathode, R1.Pin_0
  N4: LED1.anode, Componente1.D13/SCK

custom parts:
  KY-026 Flame Sensor Module: KY-026 Flame Sensor Module reacts in the presence of fire.
